# Fritzing sketch ArduinoHome (saved by Fritzing 0.9.3b)

parts:
  KY-2 = Keyes Relay [package=THT]
  Componente1 = Arduino Yun
  KY-3 = Keyes Relay [package=THT]
  KY-4 = Keyes Relay [package=THT]
  KY-5 = Keyes Relay [package=THT]
  SG1 = Buzzer 12mm [package=buzzer-ccv-kit]
  DHT1 = DHT11 Humitidy and Temperature Sensor
  R1 = Resistor [tolerance=±5% resistance=10k package=THT]
  Q1 = NPN-Transistor [part_number=2N3904 package="TO92 [THT]"]
  R2 = Resistor [tolerance=±5% resistance=10k package=THT]
  J1 = male pin header, 1 pin [form="♂ (male)"]  # not connected
  J2 = male pin header, 1 pin [form="♂ (male)"]  # not connected

nets:
  N1: KY-2.signal, Componente1.D12/MISO
  GND: KY-2.ground, Componente1.GND, DHT1.GND, Q1.E
  N2: Componente1.D8, R2.Pin_1
  N3: Componente1.D9_PWM, KY-5.signal
  N4: Componente1.D10_PWM/SS, KY-4.signal
  N5: Componente1.D11_PWM/MOSI, KY-3.signal
  N6: Componente1.D2/SDA, Componente1.D2, DHT1.DATA, R1.Pin_0
  VIN: Componente1.VIN, DHT1.VDD
  N7: KY-3.power, KY-4.power
  N8: SG1.1, Q1.C
  N9: Q1.B, R2.Pin_0

notes:
  Buzzer Alarm
  DHT11
  Room Light
  Kitchen Light
  Garage Light
  Living room Light
  Usb WebCam
  12v power
  Dc to Dc 5v power converter

custom parts:
  Keyes Relay: The Keyes 5V relay module is suitable for SCM development, home appliance control. It uses a 5V~12V TIL control signal which can control DC / AC signal.
  DHT11 Humitidy and Temperature Sensor: DHT11 Humidity and Temperature Sensor
